// Logisim project 单周期CPU.circ as structural Verilog: 9 circuits, main circuit main
module main (
  input  Reset
);

  wire aluwith9ins_1_zero, and_1_out, and_2_out, and_3_out, and_4_out, clock_1_out, control_1_alusrc,
       control_1_branch, control_1_clockout, control_1_lu, control_1_memread, control_1_memtoreg,
       control_1_memwrite, control_1_regdst, control_1_regwrite, not_1_out;
  wire [1:0] control_1_alucontrol;
  wire [3:0] count_1_count_out_2;
  wire [4:0] multiplexer_1_out;
  wire [31:0] adder_1_out, adder_2_out, aluwith9ins_1_aluresult, count_1_count_out, excontrol_1_out_32,
       IM_data, multiplexer_2_out, multiplexer_3_out, multiplexer_4_out, PC_q, ram_1_dout, reg32_1_r0,
       reg32_1_r1;

  Clock clock_1 (.out(clock_1_out));
  and and_1 (and_1_out, control_1_clockout, clock_1_out);
  Register #(.width(32)) PC (.D(multiplexer_3_out), .en(1'b1), .clk(and_1_out), .Q(PC_q), .clr(Reset));
  ROM #(.addrWidth(14), .dataWidth(32)) IM (.addr(PC_q[15:2]), .data(IM_data));
  Adder #(.width(32)) adder_1 (.a(32'h4), .b(PC_q), .out(adder_1_out), .cin(1'b0));  // open: cout
  and and_2 (and_2_out, control_1_clockout, clock_1_out);
  Multiplexer #(.width(5)) multiplexer_1 (
    .in0(IM_data[20:16]), .in1(IM_data[15:11]), .out(multiplexer_1_out), .sel(control_1_regdst));
  Hex_Digit_Display hex_digit_display_1 (.value(count_1_count_out[31:28]));  // open: dp
  Hex_Digit_Display hex_digit_display_2 (.value(count_1_count_out[27:24]));  // open: dp
  Hex_Digit_Display hex_digit_display_3 (.value(count_1_count_out_2));  // open: dp
  Hex_Digit_Display hex_digit_display_4 (.value(count_1_count_out[23:20]));  // open: dp
  Control control_1 (
    .OpCode(IM_data[31:26]), .Func(IM_data[5:0]), .RegDst(control_1_regdst), .Branch(control_1_branch),
    .MemRead(control_1_memread), .MemtoReg(control_1_memtoreg), .MemWrite(control_1_memwrite),
    .RegWrite(control_1_regwrite), .ALUControl(control_1_alucontrol), .ClockOut(control_1_clockout),
    .LU(control_1_lu), .ALUSrc(control_1_alusrc));
  Reg32 reg32_1 (
    .WEn(control_1_regwrite), .clk(and_2_out), .W(multiplexer_4_out), .W_Addr(multiplexer_1_out),
    .R_Addr0(IM_data[25:21]), .R_Addr1(IM_data[20:16]), .R0(reg32_1_r0), .R1(reg32_1_r1));
  ExControl excontrol_1 (
    .ALUControl(control_1_alucontrol), .Lui(control_1_lu), .In_16(IM_data[15:0]), .Out_32(excontrol_1_out_32));
  Hex_Digit_Display hex_digit_display_5 (.value(count_1_count_out[15:12]));  // open: dp
  Hex_Digit_Display hex_digit_display_6 (.value(count_1_count_out[11:8]));  // open: dp
  Hex_Digit_Display hex_digit_display_7 (.value(count_1_count_out[7:4]));  // open: dp
  Hex_Digit_Display hex_digit_display_8 (.value(count_1_count_out[3:0]));  // open: dp
  Count count_1 (
    .Reset(Reset), .Clk(and_1_out),
    .Count_out({count_1_count_out[31:20], count_1_count_out_2, count_1_count_out[15:0]}));
  Adder #(.width(32)) adder_2 (
    .a(adder_1_out), .b({excontrol_1_out_32[29:0], 2'b00}), .out(adder_2_out), .cin(1'b0));  // open: cout
  Multiplexer #(.width(32)) multiplexer_2 (
    .in0(reg32_1_r1), .in1(excontrol_1_out_32), .out(multiplexer_2_out), .sel(control_1_alusrc));
  Multiplexer #(.width(32)) multiplexer_3 (
    .in0(adder_1_out), .in1(adder_2_out), .out(multiplexer_3_out), .sel(and_3_out));
  and and_3 (and_3_out, control_1_branch, not_1_out);
  not not_1 (not_1_out, aluwith9ins_1_zero);
  RAM #(.addrWidth(14), .asyncread("true"), .dataWidth(32)) ram_1 (
    .addr(aluwith9ins_1_aluresult[15:2]), .we(control_1_memwrite), .oe(control_1_memread), .clk(and_4_out),
    .din(reg32_1_r1), .dout(ram_1_dout));
  and and_4 (and_4_out, clock_1_out, control_1_clockout);
  ALUwith9ins aluwith9ins_1 (
    .ALUControl(control_1_alucontrol), .ALUSource1(reg32_1_r0), .ALUSource2(multiplexer_2_out),
    .Zero(aluwith9ins_1_zero), .ALUResult(aluwith9ins_1_aluresult));
  Multiplexer #(.width(32)) multiplexer_4 (
    .in0(aluwith9ins_1_aluresult), .in1(ram_1_dout), .out(multiplexer_4_out), .sel(control_1_memtoreg));

  // Notes on the sheet:
  //   contents of IM (hex, n*v repeats v):
  //   34010001 34020001 34070004 34050100 3c080000 1053021 221821 34410000 34620000 ad020000 8d040000
  //   14440003 1074021 106482a 1520fff7 fc000000 14c0fff5
endmodule

module ALUwith9ins (
  input  [1:0] ALUControl,
  input  [31:0] ALUSource1,
  input  [31:0] ALUSource2,
  output Zero,
  output [31:0] ALUResult
);

  wire not_1_out;
  wire [1:1] and_1_out;
  wire [30:0] subtractor_1_out;
  wire [31:0] adder_1_out, demultiplexer_1_out0, demultiplexer_1_out1, demultiplexer_1_out2,
       demultiplexer_2_out0, demultiplexer_2_out1, demultiplexer_2_out2, or_1_out;
  wire [31:31] subtractor_1_out_2;

  not not_1 (not_1_out, ALUControl[0]);
  Demultiplexer #(.select(2), .width(32)) demultiplexer_1 (
    .out0(demultiplexer_1_out0), .out1(demultiplexer_1_out1), .out2(demultiplexer_1_out2), .in(ALUSource1),
    .sel({and_1_out[1], ALUControl[0]}));  // open: out3
  Demultiplexer #(.select(2), .width(32)) demultiplexer_2 (
    .out0(demultiplexer_2_out0), .out1(demultiplexer_2_out1), .out2(demultiplexer_2_out2), .in(ALUSource2),
    .sel({and_1_out[1], ALUControl[0]}));  // open: out3
  and and_1 (and_1_out[1], ALUControl[1], not_1_out);
  Adder #(.width(32)) adder_1 (
    .a(demultiplexer_1_out0), .b(demultiplexer_2_out0), .out(adder_1_out), .cin(1'b0));  // open: cout
  Subtractor #(.width(32)) subtractor_1 (
    .a(demultiplexer_1_out1), .b(demultiplexer_2_out1), .out({subtractor_1_out_2[31], subtractor_1_out}),
    .bin(1'b0));  // open: bout
  assign or_1_out = demultiplexer_1_out2 | demultiplexer_2_out2;  // OR_Gate or_1, 32 bits wide
  Multiplexer #(.select(2), .width(32)) multiplexer_1 (
    .in0(adder_1_out), .in1({subtractor_1_out_2[31], subtractor_1_out}), .in2(or_1_out),
    .in3({{31{1'b0}}, subtractor_1_out_2[31]}), .out(ALUResult), .sel(ALUControl));
  nor nor_1 (Zero, ALUResult[0], ALUResult[1], ALUResult[2], ALUResult[3], ALUResult[4], ALUResult[5], ALUResult[6], ALUResult[7], ALUResult[8], ALUResult[9], ALUResult[10], ALUResult[11], ALUResult[12], ALUResult[13], ALUResult[14], ALUResult[15], ALUResult[16], ALUResult[17], ALUResult[18], ALUResult[19], ALUResult[20], ALUResult[21], ALUResult[22], ALUResult[23], ALUResult[24], ALUResult[25], ALUResult[26], ALUResult[27], ALUResult[28], ALUResult[29], ALUResult[30], ALUResult[31]);
endmodule

module Control (
  input  [5:0] OpCode,
  input  [5:0] Func,
  output RegDst,
  output Branch,
  output MemRead,
  output MemtoReg,
  output MemWrite,
  output RegWrite,
  output [1:0] ALUControl,
  output ClockOut,
  output LU,
  output ALUSrc
);

  wire and_1_out, and_2_out, and_3_out, and_8_out, and_10_out, not_1_out, not_2_out, not_3_out, not_4_out,
       not_5_out, not_6_out, not_7_out, not_8_out, not_9_out, not_10_out, not_12_out;

  not not_1 (not_1_out, OpCode[0]);
  not not_2 (not_2_out, OpCode[1]);
  not not_3 (not_3_out, Func[0]);
  not not_4 (not_4_out, OpCode[0]);
  and and_1 (and_1_out, not_1_out, Func[3]);
  and and_2 (and_2_out, OpCode[2], OpCode[3], not_2_out);
  and and_3 (and_3_out, not_3_out, Func[1], not_4_out);
  or or_1 (ALUControl[1], and_1_out, and_2_out);
  or or_2 (ALUControl[0], Branch, and_3_out);
  not not_5 (not_5_out, OpCode[0]);
  not not_6 (not_6_out, OpCode[4]);
  and and_4 (RegDst, not_5_out, Func[5]);
  not not_7 (not_7_out, OpCode[1]);
  and and_5 (Branch, OpCode[0], not_7_out, not_8_out);
  not not_8 (not_8_out, OpCode[3]);
  not not_9 (not_9_out, OpCode[3]);
  and and_6 (MemRead, OpCode[0], not_9_out, OpCode[5]);
  not not_10 (not_10_out, OpCode[2]);
  and and_7 (MemWrite, OpCode[1], not_10_out, OpCode[3]);
  or or_3 (RegWrite, RegDst, MemRead, and_8_out);
  and and_8 (and_8_out, OpCode[2], OpCode[3], not_6_out);
  not not_11 (ClockOut, OpCode[4]);
  and and_9 (LU, OpCode[1], OpCode[2], not_12_out);
  not not_12 (not_12_out, OpCode[5]);
  or or_4 (ALUSrc, MemWrite, LU, and_10_out);
  and and_10 (and_10_out, OpCode[0], RegWrite);

  assign MemtoReg = MemRead;
endmodule

module Reg4Byte (
  input  clk,
  input  WEn,
  input  [31:0] RegIn,
  output [31:0] RegOut
);

  Register register_1 (.D(RegIn[7:0]), .en(WEn), .clk(clk), .Q(RegOut[7:0]));  // open: clr
  Register register_2 (.D(RegIn[15:8]), .en(WEn), .clk(clk), .Q(RegOut[15:8]));  // open: clr
  Register register_3 (.D(RegIn[23:16]), .en(WEn), .clk(clk), .Q(RegOut[23:16]));  // open: clr
  Register register_4 (.D(RegIn[31:24]), .en(WEn), .clk(clk), .Q(RegOut[31:24]));  // open: clr
endmodule

module Reg8 (
  input  Clk,
  input  [31:0] W,
  input  WEn,
  input  [2:0] W_Addr,
  input  [2:0] R_Addr0,
  input  [2:0] R_Addr1,
  output [31:0] R0,
  output [31:0] R1
);

  wire demultiplexer_2_out0, demultiplexer_2_out1, demultiplexer_2_out2, demultiplexer_2_out3,
       demultiplexer_2_out4, demultiplexer_2_out5, demultiplexer_2_out6, demultiplexer_2_out7;
  wire [31:0] demultiplexer_1_out0, demultiplexer_1_out1, demultiplexer_1_out2, demultiplexer_1_out3,
       demultiplexer_1_out4, demultiplexer_1_out5, demultiplexer_1_out6, demultiplexer_1_out7,
       reg4byte_1_regout, reg4byte_2_regout, reg4byte_3_regout, reg4byte_4_regout, reg4byte_5_regout,
       reg4byte_6_regout, reg4byte_7_regout, reg4byte_8_regout;

  Demultiplexer #(.select(3), .width(32)) demultiplexer_1 (
    .out0(demultiplexer_1_out0), .out1(demultiplexer_1_out1), .out2(demultiplexer_1_out2),
    .out3(demultiplexer_1_out3), .out4(demultiplexer_1_out4), .out5(demultiplexer_1_out5),
    .out6(demultiplexer_1_out6), .out7(demultiplexer_1_out7), .in(W), .sel(W_Addr));
  Demultiplexer #(.select(3)) demultiplexer_2 (
    .out0(demultiplexer_2_out0), .out1(demultiplexer_2_out1), .out2(demultiplexer_2_out2),
    .out3(demultiplexer_2_out3), .out4(demultiplexer_2_out4), .out5(demultiplexer_2_out5),
    .out6(demultiplexer_2_out6), .out7(demultiplexer_2_out7), .in(WEn), .sel(W_Addr));
  Reg4Byte reg4byte_1 (.clk(Clk), .WEn(demultiplexer_2_out0), .RegIn(demultiplexer_1_out0), .RegOut(reg4byte_1_regout));
  Reg4Byte reg4byte_2 (.clk(Clk), .WEn(demultiplexer_2_out1), .RegIn(demultiplexer_1_out1), .RegOut(reg4byte_2_regout));
  Reg4Byte reg4byte_3 (.clk(Clk), .WEn(demultiplexer_2_out2), .RegIn(demultiplexer_1_out2), .RegOut(reg4byte_3_regout));
  Reg4Byte reg4byte_4 (.clk(Clk), .WEn(demultiplexer_2_out3), .RegIn(demultiplexer_1_out3), .RegOut(reg4byte_4_regout));
  Reg4Byte reg4byte_5 (.clk(Clk), .WEn(demultiplexer_2_out4), .RegIn(demultiplexer_1_out4), .RegOut(reg4byte_5_regout));
  Reg4Byte reg4byte_6 (.clk(Clk), .WEn(demultiplexer_2_out5), .RegIn(demultiplexer_1_out5), .RegOut(reg4byte_6_regout));
  Reg4Byte reg4byte_7 (.clk(Clk), .WEn(demultiplexer_2_out6), .RegIn(demultiplexer_1_out6), .RegOut(reg4byte_7_regout));
  Reg4Byte reg4byte_8 (.clk(Clk), .WEn(demultiplexer_2_out7), .RegIn(demultiplexer_1_out7), .RegOut(reg4byte_8_regout));
  Multiplexer #(.select(3), .width(32)) multiplexer_1 (
    .in0(reg4byte_1_regout), .in1(reg4byte_2_regout), .in2(reg4byte_3_regout), .in3(reg4byte_4_regout),
    .in4(reg4byte_5_regout), .in5(reg4byte_6_regout), .in6(reg4byte_7_regout), .in7(reg4byte_8_regout),
    .out(R0), .sel(R_Addr0));
  Multiplexer #(.select(3), .width(32)) multiplexer_2 (
    .in0(reg4byte_1_regout), .in1(reg4byte_2_regout), .in2(reg4byte_3_regout), .in3(reg4byte_4_regout),
    .in4(reg4byte_5_regout), .in5(reg4byte_6_regout), .in6(reg4byte_7_regout), .in7(reg4byte_8_regout),
    .out(R1), .sel(R_Addr1));
endmodule

module Reg32 (
  input  WEn,
  input  clk,
  input  [31:0] W,
  input  [4:0] W_Addr,
  input  [4:0] R_Addr0,
  input  [4:0] R_Addr1,
  output [31:0] R0,
  output [31:0] R1
);

  wire demultiplexer_1_out0, demultiplexer_1_out1, demultiplexer_1_out2, demultiplexer_1_out3;
  wire [31:0] demultiplexer_2_out0, demultiplexer_2_out1, demultiplexer_2_out2, demultiplexer_2_out3,
       reg8_1_r0, reg8_1_r1, reg8_2_r0, reg8_2_r1, reg8_3_r0, reg8_3_r1, reg8_first_1_r0, reg8_first_1_r1;

  Demultiplexer #(.select(2)) demultiplexer_1 (
    .out0(demultiplexer_1_out0), .out1(demultiplexer_1_out1), .out2(demultiplexer_1_out2),
    .out3(demultiplexer_1_out3), .in(WEn), .sel(W_Addr[4:3]));
  Demultiplexer #(.select(2), .width(32)) demultiplexer_2 (
    .out0(demultiplexer_2_out0), .out1(demultiplexer_2_out1), .out2(demultiplexer_2_out2),
    .out3(demultiplexer_2_out3), .in(W), .sel(W_Addr[4:3]));
  Reg8_First reg8_first_1 (
    .Clk(clk), .W(demultiplexer_2_out0), .WEn(demultiplexer_1_out0), .W_Addr(W_Addr[2:0]),
    .R_Addr0(R_Addr0[2:0]), .R_Addr1(R_Addr1[2:0]), .R0(reg8_first_1_r0), .R1(reg8_first_1_r1));
  Reg8 reg8_1 (
    .Clk(clk), .W(demultiplexer_2_out1), .WEn(demultiplexer_1_out1), .W_Addr(W_Addr[2:0]),
    .R_Addr0(R_Addr0[2:0]), .R_Addr1(R_Addr1[2:0]), .R0(reg8_1_r0), .R1(reg8_1_r1));
  Reg8 reg8_2 (
    .Clk(clk), .W(demultiplexer_2_out2), .WEn(demultiplexer_1_out2), .W_Addr(W_Addr[2:0]),
    .R_Addr0(R_Addr0[2:0]), .R_Addr1(R_Addr1[2:0]), .R0(reg8_2_r0), .R1(reg8_2_r1));
  Reg8 reg8_3 (
    .Clk(clk), .W(demultiplexer_2_out3), .WEn(demultiplexer_1_out3), .W_Addr(W_Addr[2:0]),
    .R_Addr0(R_Addr0[2:0]), .R_Addr1(R_Addr1[2:0]), .R0(reg8_3_r0), .R1(reg8_3_r1));
  Multiplexer #(.select(2), .width(32)) multiplexer_1 (
    .in0(reg8_first_1_r0), .in1(reg8_1_r0), .in2(reg8_2_r0), .in3(reg8_3_r0), .out(R0), .sel(R_Addr0[4:3]));
  Multiplexer #(.select(2), .width(32)) multiplexer_2 (
    .in0(reg8_first_1_r1), .in1(reg8_1_r1), .in2(reg8_2_r1), .in3(reg8_3_r1), .out(R1), .sel(R_Addr1[4:3]));
endmodule

module Count (
  input  Reset,
  input  Clk,
  output [31:0] Count_out
);

  wire [31:0] adder_1_out;

  Adder #(.width(32)) adder_1 (.a(Count_out), .b({32{1'b0}}), .out(adder_1_out), .cin(1'b1));  // open: cout
  Register #(.width(32)) register_1 (.D(adder_1_out), .en(1'b1), .clk(Clk), .Q(Count_out), .clr(Reset));
endmodule

module ExControl (
  input  [1:0] ALUControl,
  input  Lui,
  input  [15:0] In_16,
  output [31:0] Out_32
);

  wire not_1_out, not_2_out, not_3_out, not_4_out;
  wire [1:0] and_2_out;

  not not_1 (not_1_out, ALUControl[0]);
  not not_2 (not_2_out, ALUControl[1]);
  not not_3 (not_3_out, ALUControl[0]);
  not not_4 (not_4_out, Lui);
  and and_1 (and_2_out[1], not_1_out, not_2_out, Lui);
  and and_2 (and_2_out[0], not_3_out, ALUControl[1], not_4_out);
  Multiplexer #(.select(2), .width(32)) multiplexer_1 (
    .in0({{17{In_16[15]}}, In_16[14:0]}), .in1({{16{1'b0}}, In_16}), .in2({In_16, {16{1'b0}}}), .out(Out_32),
    .sel(and_2_out));  // open: in3
endmodule

module Reg8_First (
  input  Clk,
  input  [31:0] W,
  input  WEn,
  input  [2:0] W_Addr,
  input  [2:0] R_Addr0,
  input  [2:0] R_Addr1,
  output [31:0] R0,
  output [31:0] R1
);

  wire demultiplexer_2_out0, demultiplexer_2_out1, demultiplexer_2_out2, demultiplexer_2_out3,
       demultiplexer_2_out4, demultiplexer_2_out5, demultiplexer_2_out6, demultiplexer_2_out7;
  wire [31:0] demultiplexer_1_out0, demultiplexer_1_out1, demultiplexer_1_out2, demultiplexer_1_out3,
       demultiplexer_1_out4, demultiplexer_1_out5, demultiplexer_1_out6, demultiplexer_1_out7,
       reg4byte_1_regout, reg4byte_2_regout, reg4byte_3_regout, reg4byte_4_regout, reg4byte_5_regout,
       reg4byte_6_regout, reg4byte_7_regout;

  Demultiplexer #(.select(3), .width(32)) demultiplexer_1 (
    .out0(demultiplexer_1_out0), .out1(demultiplexer_1_out1), .out2(demultiplexer_1_out2),
    .out3(demultiplexer_1_out3), .out4(demultiplexer_1_out4), .out5(demultiplexer_1_out5),
    .out6(demultiplexer_1_out6), .out7(demultiplexer_1_out7), .in(W), .sel(W_Addr));
  Demultiplexer #(.select(3)) demultiplexer_2 (
    .out0(demultiplexer_2_out0), .out1(demultiplexer_2_out1), .out2(demultiplexer_2_out2),
    .out3(demultiplexer_2_out3), .out4(demultiplexer_2_out4), .out5(demultiplexer_2_out5),
    .out6(demultiplexer_2_out6), .out7(demultiplexer_2_out7), .in(WEn), .sel(W_Addr));
  Reg4Byte reg4byte_1 (.clk(Clk), .WEn(demultiplexer_2_out1), .RegIn(demultiplexer_1_out1), .RegOut(reg4byte_1_regout));
  Reg4Byte reg4byte_2 (.clk(Clk), .WEn(demultiplexer_2_out2), .RegIn(demultiplexer_1_out2), .RegOut(reg4byte_2_regout));
  Reg4Byte reg4byte_3 (.clk(Clk), .WEn(demultiplexer_2_out3), .RegIn(demultiplexer_1_out3), .RegOut(reg4byte_3_regout));
  Reg4Byte reg4byte_4 (.clk(Clk), .WEn(demultiplexer_2_out4), .RegIn(demultiplexer_1_out4), .RegOut(reg4byte_4_regout));
  Reg4Byte reg4byte_5 (.clk(Clk), .WEn(demultiplexer_2_out5), .RegIn(demultiplexer_1_out5), .RegOut(reg4byte_5_regout));
  Reg4Byte reg4byte_6 (.clk(Clk), .WEn(demultiplexer_2_out6), .RegIn(demultiplexer_1_out6), .RegOut(reg4byte_6_regout));
  Reg4Byte reg4byte_7 (.clk(Clk), .WEn(demultiplexer_2_out7), .RegIn(demultiplexer_1_out7), .RegOut(reg4byte_7_regout));
  Multiplexer #(.select(3), .width(32)) multiplexer_1 (
    .in0({32{1'b0}}), .in1(reg4byte_1_regout), .in2(reg4byte_2_regout), .in3(reg4byte_3_regout),
    .in4(reg4byte_4_regout), .in5(reg4byte_5_regout), .in6(reg4byte_6_regout), .in7(reg4byte_7_regout),
    .out(R0), .sel(R_Addr0));
  Multiplexer #(.select(3), .width(32)) multiplexer_2 (
    .in0({32{1'b0}}), .in1(reg4byte_1_regout), .in2(reg4byte_2_regout), .in3(reg4byte_3_regout),
    .in4(reg4byte_4_regout), .in5(reg4byte_5_regout), .in6(reg4byte_6_regout), .in7(reg4byte_7_regout),
    .out(R1), .sel(R_Addr1));
endmodule
