// Logisim project 流水线CPU_BTB.circ as structural Verilog: 12 circuits, main circuit main
module main (
  input  Reset
);

  wire and_1_out, and_2_out, and_3_out, clock_1_out, conflictdetecter_1_lu_stall, control_1_lu, not_1_out,
       or_1_out, or_2_out;
  wire [2:0] conflictdetecter_1_r0_sel, conflictdetecter_1_r1_sel, WB_Crtl_q;
  wire [4:0] EX_Mem_1_q, Mem_WB_1_q, multiplexer_5_out, WB_Mem_Ctrl_q;
  wire [8:0] control_1_regdst, multiplexer_3_out, WB_Mem_EX_Crtl_q;
  wire [9:0] ID_EX_2_q, IF_ID_0_q_2;
  wire [31:0] aluwith9ins_1_aluresult, btb_1_cmd_out, btb_1_pc_nextaddr, count_1_count_out,
       excontrol_1_out_32, ID_EX_1_q, IF_ID_0_q, IM_data, multiplexer_4_out, multiplexer_6_out, PC_q,
       ram_1_dout, reg32_1_r0, reg32_1_r1;
  wire [63:0] EX_Mem_0_q, ID_EX_0_q, Mem_WB_0_q, multiplexer_2_out;

  Clock clock_1 (.out(clock_1_out));
  Register #(.width(32)) PC (.D(btb_1_pc_nextaddr), .en(not_1_out), .clk(and_1_out), .Q(PC_q), .clr(Reset));
  ROM #(.addrWidth(14), .dataWidth(32)) IM (.addr(PC_q[15:2]), .data(IM_data));
  or or_1 (or_1_out, control_1_regdst[8], Reset);
  and and_1 (and_1_out, clock_1_out, or_1_out);
  BTB btb_1 (
    .Clk(clock_1_out), .CMD_Addr(PC_q), .CMD_In(IM_data), .ID_R0(multiplexer_2_out[31:0]),
    .ID_R1(multiplexer_2_out[63:32]), .Lu_Stall(conflictdetecter_1_lu_stall), .CMD_Out(btb_1_cmd_out),
    .PC_NextAddr(btb_1_pc_nextaddr));
  Register #(.width(32)) IF_ID_0 (
    .D(btb_1_cmd_out), .en(not_1_out), .clk(and_1_out),
    .Q({IF_ID_0_q[31:21], IF_ID_0_q_2[4:0], IF_ID_0_q_2[9:5], IF_ID_0_q[10:0]}));  // open: clr
  and and_2 (and_2_out, clock_1_out, WB_Crtl_q[0]);
  or or_2 (or_2_out, and_1_out, and_2_out);
  Control control_1 (
    .OpCode(IF_ID_0_q[31:26]), .Func(IF_ID_0_q[5:0]), .RegDst(control_1_regdst[0]),
    .MemRead(control_1_regdst[1]), .MemtoReg(control_1_regdst[2]), .MemWrite(control_1_regdst[3]),
    .RegWrite(control_1_regdst[4]), .ALUControl(control_1_regdst[6:5]), .ClockOut(control_1_regdst[8]),
    .LU(control_1_lu), .ALUSrc(control_1_regdst[7]));  // open: Branch
  Reg32 reg32_1 (
    .WEn(WB_Crtl_q[2]), .clk(and_2_out), .W(multiplexer_6_out), .W_Addr(Mem_WB_1_q),
    .R_Addr0(IF_ID_0_q[25:21]), .R_Addr1(IF_ID_0_q_2[4:0]), .R0(reg32_1_r0), .R1(reg32_1_r1));
  ExControl excontrol_1 (
    .ALUControl(control_1_regdst[6:5]), .Lui(control_1_lu), .In_16({IF_ID_0_q_2[9:5], IF_ID_0_q[10:0]}),
    .Out_32(excontrol_1_out_32));
  Count count_1 (.Reset(Reset), .Clk(or_2_out), .Count_out(count_1_count_out));
  LED led_1 (.in(control_1_regdst[8]));
  not not_1 (not_1_out, conflictdetecter_1_lu_stall);
  Multiplexer #(.select(3), .width(32)) multiplexer_1 (
    .in0(reg32_1_r1), .in1(multiplexer_6_out), .in2(EX_Mem_0_q[31:0]), .in3(aluwith9ins_1_aluresult),
    .in4(ram_1_dout), .in7(aluwith9ins_1_aluresult), .out(multiplexer_2_out[63:32]),
    .sel(conflictdetecter_1_r1_sel));  // open: in5, in6
  Multiplexer #(.select(3), .width(32)) multiplexer_2 (
    .in0(reg32_1_r0), .in1(multiplexer_6_out), .in2(EX_Mem_0_q[31:0]), .in4(ram_1_dout),
    .in7(aluwith9ins_1_aluresult), .out(multiplexer_2_out[31:0]), .sel(conflictdetecter_1_r0_sel));  // open: in3, in5, in6
  Hex_Digit_Display hex_digit_display_1 (.value(count_1_count_out[31:28]));  // open: dp
  Hex_Digit_Display hex_digit_display_2 (.value(count_1_count_out[27:24]));  // open: dp
  Register #(.width(9)) WB_Mem_EX_Crtl (
    .D(multiplexer_3_out), .en(1'b1), .clk(clock_1_out), .Q(WB_Mem_EX_Crtl_q));  // open: clr
  Multiplexer #(.width(9)) multiplexer_3 (
    .in0(control_1_regdst), .in1(9'h100), .out(multiplexer_3_out), .sel(conflictdetecter_1_lu_stall));
  Register #(.width(64)) ID_EX_0 (.D(multiplexer_2_out), .en(1'b1), .clk(clock_1_out), .Q(ID_EX_0_q));  // open: clr
  Register #(.width(32)) ID_EX_1 (.D(excontrol_1_out_32), .en(1'b1), .clk(clock_1_out), .Q(ID_EX_1_q));  // open: clr
  Register #(.width(10)) ID_EX_2 (.D(IF_ID_0_q_2), .en(1'b1), .clk(clock_1_out), .Q(ID_EX_2_q));  // open: clr
  Hex_Digit_Display hex_digit_display_3 (.value(count_1_count_out[23:20]));  // open: dp
  Hex_Digit_Display hex_digit_display_4 (.value(count_1_count_out[19:16]));  // open: dp
  Hex_Digit_Display hex_digit_display_5 (.value(count_1_count_out[15:12]));  // open: dp
  Hex_Digit_Display hex_digit_display_6 (.value(count_1_count_out[11:8]));  // open: dp
  Hex_Digit_Display hex_digit_display_7 (.value(count_1_count_out[7:4]));  // open: dp
  Hex_Digit_Display hex_digit_display_8 (.value(count_1_count_out[3:0]));  // open: dp
  Multiplexer #(.width(32)) multiplexer_4 (
    .in0(ID_EX_0_q[63:32]), .in1(ID_EX_1_q), .out(multiplexer_4_out), .sel(WB_Mem_EX_Crtl_q[7]));
  Multiplexer #(.width(5)) multiplexer_5 (
    .in0(ID_EX_2_q[4:0]), .in1(ID_EX_2_q[9:5]), .out(multiplexer_5_out), .sel(WB_Mem_EX_Crtl_q[0]));
  LED led_2 (.in(WB_Mem_EX_Crtl_q[8]));
  ALUwith9ins aluwith9ins_1 (
    .ALUControl(WB_Mem_EX_Crtl_q[6:5]), .ALUSource1(ID_EX_0_q[31:0]), .ALUSource2(multiplexer_4_out),
    .ALUResult(aluwith9ins_1_aluresult));
  ConflictDetecter conflictdetecter_1 (
    .WB_Addr(Mem_WB_1_q), .EX_WAddr(multiplexer_5_out), .Mem_WAddr(EX_Mem_1_q), .ID_R0Addr(IF_ID_0_q[25:21]),
    .ID_R1Addr(IF_ID_0_q_2[4:0]), .Mem_RegW(WB_Mem_Ctrl_q[3]), .Ex_RegW(WB_Mem_EX_Crtl_q[4]),
    .WB_RegW(WB_Crtl_q[2]), .MemW(control_1_regdst[4]), .Ex_MemR(WB_Mem_EX_Crtl_q[1]), .Clk(clock_1_out),
    .R1_Sel(conflictdetecter_1_r1_sel), .R0_Sel(conflictdetecter_1_r0_sel),
    .LU_Stall(conflictdetecter_1_lu_stall));
  Register #(.width(5)) WB_Mem_Ctrl (
    .D({WB_Mem_EX_Crtl_q[8], WB_Mem_EX_Crtl_q[4:1]}), .en(1'b1), .clk(clock_1_out), .Q(WB_Mem_Ctrl_q));  // open: clr
  Register #(.width(64)) EX_Mem_0 (
    .D({ID_EX_0_q[63:32], aluwith9ins_1_aluresult}), .en(1'b1), .clk(clock_1_out), .Q(EX_Mem_0_q));  // open: clr
  Register #(.width(5)) EX_Mem_1 (.D(multiplexer_5_out), .en(1'b1), .clk(clock_1_out), .Q(EX_Mem_1_q));  // open: clr
  and and_3 (and_3_out, WB_Mem_Ctrl_q[4], clock_1_out);
  RAM #(.addrWidth(14), .asyncread("true"), .dataWidth(32)) ram_1 (
    .addr(EX_Mem_0_q[15:2]), .we(WB_Mem_Ctrl_q[2]), .oe(WB_Mem_Ctrl_q[0]), .clk(and_3_out),
    .din(EX_Mem_0_q[63:32]), .dout(ram_1_dout));
  LED led_3 (.in(WB_Mem_Ctrl_q[4]));
  Register #(.width(3)) WB_Crtl (
    .D({WB_Mem_Ctrl_q[3], WB_Mem_Ctrl_q[1], WB_Mem_Ctrl_q[4]}), .en(1'b1), .clk(clock_1_out), .Q(WB_Crtl_q));  // open: clr
  Register #(.width(64)) Mem_WB_0 (
    .D({ram_1_dout, EX_Mem_0_q[31:0]}), .en(1'b1), .clk(clock_1_out), .Q(Mem_WB_0_q));  // open: clr
  Register #(.width(5)) Mem_WB_1 (.D(EX_Mem_1_q), .en(1'b1), .clk(clock_1_out), .Q(Mem_WB_1_q));  // open: clr
  LED led_4 (.in(WB_Crtl_q[0]));
  Multiplexer #(.width(32)) multiplexer_6 (
    .in0(Mem_WB_0_q[31:0]), .in1(Mem_WB_0_q[63:32]), .out(multiplexer_6_out), .sel(WB_Crtl_q[1]));

  // Notes on the sheet:
  //   contents of IM (hex, n*v repeats v):
  //   34010001 34020001 34070004 34050100 3c080000 1053021 221821 34410000 34620000 ad020000 8d040000
  //   14440003 1074021 106482a 1520fff7 fc000000 14c0fff5
endmodule

module ConflictDetecter (
  input  [4:0] WB_Addr,
  input  [4:0] EX_WAddr,
  input  [4:0] Mem_WAddr,
  input  [4:0] ID_R0Addr,
  input  [4:0] ID_R1Addr,
  input  Mem_RegW,
  input  Ex_RegW,
  input  WB_RegW,
  input  MemW,
  input  Ex_MemR,
  input  Clk,
  output [2:0] R1_Sel,
  output [2:0] R0_Sel,
  output LU_Stall
);

  wire and_2_out, and_3_out, and_4_out, and_5_out, and_6_out, and_7_out, and_8_out, and_9_out, and_10_out,
       comparator_1_eq, comparator_2_eq, comparator_3_eq, comparator_4_eq, comparator_5_eq, comparator_6_eq,
       comparator_7_eq, comparator_8_eq, d_ff_1_q, nor_1_out, nor_2_out, not_1_out, not_2_out, or_1_out;

  Comparator #(.width(5)) comparator_1 (.a(ID_R0Addr), .b({5{1'b0}}), .eq(comparator_1_eq));  // open: gt, lt
  Comparator #(.width(5)) comparator_2 (.a(ID_R1Addr), .b({5{1'b0}}), .eq(comparator_2_eq));  // open: gt, lt
  not not_1 (not_1_out, comparator_2_eq);
  not not_2 (not_2_out, comparator_1_eq);
  Comparator #(.width(5)) comparator_3 (.a(WB_Addr), .b(ID_R0Addr), .eq(comparator_3_eq));  // open: gt, lt
  Comparator #(.width(5)) comparator_4 (.a(EX_WAddr), .b(ID_R0Addr), .eq(comparator_4_eq));  // open: gt, lt
  Comparator #(.width(5)) comparator_5 (.a(Mem_WAddr), .b(ID_R0Addr), .eq(comparator_5_eq));  // open: gt, lt
  Comparator #(.width(5)) comparator_6 (.a(WB_Addr), .b(ID_R1Addr), .eq(comparator_6_eq));  // open: gt, lt
  Comparator #(.width(5)) comparator_7 (.a(EX_WAddr), .b(ID_R1Addr), .eq(comparator_7_eq));  // open: gt, lt
  Comparator #(.width(5)) comparator_8 (.a(Mem_WAddr), .b(ID_R1Addr), .eq(comparator_8_eq));  // open: gt, lt
  or or_1 (or_1_out, comparator_4_eq, comparator_7_eq);
  and and_1 (LU_Stall, or_1_out, Ex_MemR);
  and and_2 (and_2_out, not_1_out, comparator_6_eq, WB_RegW);
  and and_3 (and_3_out, comparator_7_eq, not_1_out, MemW, Ex_RegW);
  and and_4 (and_4_out, not_1_out, comparator_7_eq, Ex_RegW);
  and and_5 (and_5_out, not_1_out, Mem_RegW, comparator_8_eq);
  and and_6 (and_6_out, WB_RegW, comparator_3_eq, not_2_out);
  and and_7 (and_7_out, Mem_RegW, comparator_5_eq, not_2_out);
  and and_8 (and_8_out, Ex_RegW, comparator_4_eq, not_2_out);
  D_Flip_Flop d_ff_1 (.D(LU_Stall), .clk(Clk), .Q(d_ff_1_q));  // open: Qn, preset, reset
  nor nor_1 (nor_1_out, and_2_out, and_3_out, and_9_out, and_5_out, and_4_out);
  and and_9 (and_9_out, comparator_7_eq, d_ff_1_q);
  and and_10 (and_10_out, comparator_4_eq, d_ff_1_q);
  nor nor_2 (nor_2_out, and_6_out, and_10_out, and_7_out, and_8_out);
  Priority_Encoder priority_encoder_1 (
    .in0(nor_1_out), .in1(and_2_out), .in2(and_5_out), .in3(and_3_out), .in4(and_9_out), .in7(and_4_out),
    .out(R1_Sel));  // open: in5, in6, en_in, gs, en_out
  Priority_Encoder priority_encoder_2 (
    .in0(nor_2_out), .in1(and_6_out), .in2(and_7_out), .in4(and_10_out), .in7(and_8_out), .out(R0_Sel));  // open: in3, in5, in6, en_in, gs, en_out
endmodule

module ALUwith9ins (
  input  [1:0] ALUControl,
  input  [31:0] ALUSource1,
  input  [31:0] ALUSource2,
  output [31:0] ALUResult
);

  wire not_1_out;
  wire [1:1] and_1_out;
  wire [30:0] subtractor_1_out;
  wire [31:0] adder_1_out, demultiplexer_1_out0, demultiplexer_1_out1, demultiplexer_1_out2,
       demultiplexer_2_out0, demultiplexer_2_out1, demultiplexer_2_out2, or_1_out;
  wire [31:31] subtractor_1_out_2;

  not not_1 (not_1_out, ALUControl[0]);
  Demultiplexer #(.select(2), .width(32)) demultiplexer_1 (
    .out0(demultiplexer_1_out0), .out1(demultiplexer_1_out1), .out2(demultiplexer_1_out2), .in(ALUSource1),
    .sel({and_1_out[1], ALUControl[0]}));  // open: out3
  Demultiplexer #(.select(2), .width(32)) demultiplexer_2 (
    .out0(demultiplexer_2_out0), .out1(demultiplexer_2_out1), .out2(demultiplexer_2_out2), .in(ALUSource2),
    .sel({and_1_out[1], ALUControl[0]}));  // open: out3
  and and_1 (and_1_out[1], ALUControl[1], not_1_out);
  Adder #(.width(32)) adder_1 (
    .a(demultiplexer_1_out0), .b(demultiplexer_2_out0), .out(adder_1_out), .cin(1'b0));  // open: cout
  Subtractor #(.width(32)) subtractor_1 (
    .a(demultiplexer_1_out1), .b(demultiplexer_2_out1), .out({subtractor_1_out_2[31], subtractor_1_out}),
    .bin(1'b0));  // open: bout
  assign or_1_out = demultiplexer_1_out2 | demultiplexer_2_out2;  // OR_Gate or_1, 32 bits wide
  Multiplexer #(.select(2), .width(32)) multiplexer_1 (
    .in0(adder_1_out), .in1({subtractor_1_out_2[31], subtractor_1_out}), .in2(or_1_out),
    .in3({{31{1'b0}}, subtractor_1_out_2[31]}), .out(ALUResult), .sel(ALUControl));
endmodule

module Control (
  input  [5:0] OpCode,
  input  [5:0] Func,
  output Branch,
  output RegDst,
  output MemRead,
  output MemtoReg,
  output MemWrite,
  output RegWrite,
  output [1:0] ALUControl,
  output ClockOut,
  output LU,
  output ALUSrc
);

  wire and_1_out, and_2_out, and_3_out, and_8_out, and_10_out, not_1_out, not_2_out, not_3_out, not_4_out,
       not_5_out, not_6_out, not_7_out, not_8_out, not_9_out, not_10_out, not_12_out;

  not not_1 (not_1_out, OpCode[0]);
  not not_2 (not_2_out, OpCode[1]);
  not not_3 (not_3_out, Func[0]);
  not not_4 (not_4_out, OpCode[0]);
  and and_1 (and_1_out, not_1_out, Func[3]);
  and and_2 (and_2_out, OpCode[2], OpCode[3], not_2_out);
  and and_3 (and_3_out, not_3_out, Func[1], not_4_out);
  or or_1 (ALUControl[1], and_1_out, and_2_out);
  or or_2 (ALUControl[0], Branch, and_3_out);
  not not_5 (not_5_out, OpCode[0]);
  not not_6 (not_6_out, OpCode[4]);
  and and_4 (RegDst, not_5_out, Func[5]);
  not not_7 (not_7_out, OpCode[1]);
  and and_5 (Branch, OpCode[0], not_7_out, not_8_out);
  not not_8 (not_8_out, OpCode[3]);
  not not_9 (not_9_out, OpCode[3]);
  and and_6 (MemRead, OpCode[0], not_9_out, OpCode[5]);
  not not_10 (not_10_out, OpCode[2]);
  and and_7 (MemWrite, OpCode[1], not_10_out, OpCode[3]);
  or or_3 (RegWrite, RegDst, MemRead, and_8_out);
  and and_8 (and_8_out, OpCode[2], OpCode[3], not_6_out);
  not not_11 (ClockOut, OpCode[4]);
  and and_9 (LU, OpCode[1], OpCode[2], not_12_out);
  not not_12 (not_12_out, OpCode[5]);
  or or_4 (ALUSrc, MemWrite, LU, and_10_out);
  and and_10 (and_10_out, OpCode[0], RegWrite);

  assign MemtoReg = MemRead;
endmodule

module Reg4Byte (
  input  clk,
  input  WEn,
  input  [31:0] RegIn,
  output [31:0] RegOut
);

  Register register_1 (.D(RegIn[7:0]), .en(WEn), .clk(clk), .Q(RegOut[7:0]));  // open: clr
  Register register_2 (.D(RegIn[15:8]), .en(WEn), .clk(clk), .Q(RegOut[15:8]));  // open: clr
  Register register_3 (.D(RegIn[23:16]), .en(WEn), .clk(clk), .Q(RegOut[23:16]));  // open: clr
  Register register_4 (.D(RegIn[31:24]), .en(WEn), .clk(clk), .Q(RegOut[31:24]));  // open: clr
endmodule

module Reg8 (
  input  Clk,
  input  [31:0] W,
  input  WEn,
  input  [2:0] W_Addr,
  input  [2:0] R_Addr0,
  input  [2:0] R_Addr1,
  output [31:0] R0,
  output [31:0] R1
);

  wire demultiplexer_2_out0, demultiplexer_2_out1, demultiplexer_2_out2, demultiplexer_2_out3,
       demultiplexer_2_out4, demultiplexer_2_out5, demultiplexer_2_out6, demultiplexer_2_out7;
  wire [31:0] demultiplexer_1_out0, demultiplexer_1_out1, demultiplexer_1_out2, demultiplexer_1_out3,
       demultiplexer_1_out4, demultiplexer_1_out5, demultiplexer_1_out6, demultiplexer_1_out7,
       reg4byte_1_regout, reg4byte_2_regout, reg4byte_3_regout, reg4byte_4_regout, reg4byte_5_regout,
       reg4byte_6_regout, reg4byte_7_regout, reg4byte_8_regout;

  Demultiplexer #(.select(3), .width(32)) demultiplexer_1 (
    .out0(demultiplexer_1_out0), .out1(demultiplexer_1_out1), .out2(demultiplexer_1_out2),
    .out3(demultiplexer_1_out3), .out4(demultiplexer_1_out4), .out5(demultiplexer_1_out5),
    .out6(demultiplexer_1_out6), .out7(demultiplexer_1_out7), .in(W), .sel(W_Addr));
  Demultiplexer #(.select(3)) demultiplexer_2 (
    .out0(demultiplexer_2_out0), .out1(demultiplexer_2_out1), .out2(demultiplexer_2_out2),
    .out3(demultiplexer_2_out3), .out4(demultiplexer_2_out4), .out5(demultiplexer_2_out5),
    .out6(demultiplexer_2_out6), .out7(demultiplexer_2_out7), .in(WEn), .sel(W_Addr));
  Reg4Byte reg4byte_1 (.clk(Clk), .WEn(demultiplexer_2_out0), .RegIn(demultiplexer_1_out0), .RegOut(reg4byte_1_regout));
  Reg4Byte reg4byte_2 (.clk(Clk), .WEn(demultiplexer_2_out1), .RegIn(demultiplexer_1_out1), .RegOut(reg4byte_2_regout));
  Reg4Byte reg4byte_3 (.clk(Clk), .WEn(demultiplexer_2_out2), .RegIn(demultiplexer_1_out2), .RegOut(reg4byte_3_regout));
  Reg4Byte reg4byte_4 (.clk(Clk), .WEn(demultiplexer_2_out3), .RegIn(demultiplexer_1_out3), .RegOut(reg4byte_4_regout));
  Reg4Byte reg4byte_5 (.clk(Clk), .WEn(demultiplexer_2_out4), .RegIn(demultiplexer_1_out4), .RegOut(reg4byte_5_regout));
  Reg4Byte reg4byte_6 (.clk(Clk), .WEn(demultiplexer_2_out5), .RegIn(demultiplexer_1_out5), .RegOut(reg4byte_6_regout));
  Reg4Byte reg4byte_7 (.clk(Clk), .WEn(demultiplexer_2_out6), .RegIn(demultiplexer_1_out6), .RegOut(reg4byte_7_regout));
  Reg4Byte reg4byte_8 (.clk(Clk), .WEn(demultiplexer_2_out7), .RegIn(demultiplexer_1_out7), .RegOut(reg4byte_8_regout));
  Multiplexer #(.select(3), .width(32)) multiplexer_1 (
    .in0(reg4byte_1_regout), .in1(reg4byte_2_regout), .in2(reg4byte_3_regout), .in3(reg4byte_4_regout),
    .in4(reg4byte_5_regout), .in5(reg4byte_6_regout), .in6(reg4byte_7_regout), .in7(reg4byte_8_regout),
    .out(R0), .sel(R_Addr0));
  Multiplexer #(.select(3), .width(32)) multiplexer_2 (
    .in0(reg4byte_1_regout), .in1(reg4byte_2_regout), .in2(reg4byte_3_regout), .in3(reg4byte_4_regout),
    .in4(reg4byte_5_regout), .in5(reg4byte_6_regout), .in6(reg4byte_7_regout), .in7(reg4byte_8_regout),
    .out(R1), .sel(R_Addr1));
endmodule

module Reg32 (
  input  WEn,
  input  clk,
  input  [31:0] W,
  input  [4:0] W_Addr,
  input  [4:0] R_Addr0,
  input  [4:0] R_Addr1,
  output [31:0] R0,
  output [31:0] R1
);

  wire demultiplexer_1_out0, demultiplexer_1_out1, demultiplexer_1_out2, demultiplexer_1_out3;
  wire [31:0] demultiplexer_2_out0, demultiplexer_2_out1, demultiplexer_2_out2, demultiplexer_2_out3,
       reg8_1_r0, reg8_1_r1, reg8_2_r0, reg8_2_r1, reg8_3_r0, reg8_3_r1, reg8_first_1_r0, reg8_first_1_r1;

  Demultiplexer #(.select(2)) demultiplexer_1 (
    .out0(demultiplexer_1_out0), .out1(demultiplexer_1_out1), .out2(demultiplexer_1_out2),
    .out3(demultiplexer_1_out3), .in(WEn), .sel(W_Addr[4:3]));
  Demultiplexer #(.select(2), .width(32)) demultiplexer_2 (
    .out0(demultiplexer_2_out0), .out1(demultiplexer_2_out1), .out2(demultiplexer_2_out2),
    .out3(demultiplexer_2_out3), .in(W), .sel(W_Addr[4:3]));
  Reg8_First reg8_first_1 (
    .Clk(clk), .W(demultiplexer_2_out0), .WEn(demultiplexer_1_out0), .W_Addr(W_Addr[2:0]),
    .R_Addr0(R_Addr0[2:0]), .R_Addr1(R_Addr1[2:0]), .R0(reg8_first_1_r0), .R1(reg8_first_1_r1));
  Reg8 reg8_1 (
    .Clk(clk), .W(demultiplexer_2_out1), .WEn(demultiplexer_1_out1), .W_Addr(W_Addr[2:0]),
    .R_Addr0(R_Addr0[2:0]), .R_Addr1(R_Addr1[2:0]), .R0(reg8_1_r0), .R1(reg8_1_r1));
  Reg8 reg8_2 (
    .Clk(clk), .W(demultiplexer_2_out2), .WEn(demultiplexer_1_out2), .W_Addr(W_Addr[2:0]),
    .R_Addr0(R_Addr0[2:0]), .R_Addr1(R_Addr1[2:0]), .R0(reg8_2_r0), .R1(reg8_2_r1));
  Reg8 reg8_3 (
    .Clk(clk), .W(demultiplexer_2_out3), .WEn(demultiplexer_1_out3), .W_Addr(W_Addr[2:0]),
    .R_Addr0(R_Addr0[2:0]), .R_Addr1(R_Addr1[2:0]), .R0(reg8_3_r0), .R1(reg8_3_r1));
  Multiplexer #(.select(2), .width(32)) multiplexer_1 (
    .in0(reg8_first_1_r0), .in1(reg8_1_r0), .in2(reg8_2_r0), .in3(reg8_3_r0), .out(R0), .sel(R_Addr0[4:3]));
  Multiplexer #(.select(2), .width(32)) multiplexer_2 (
    .in0(reg8_first_1_r1), .in1(reg8_1_r1), .in2(reg8_2_r1), .in3(reg8_3_r1), .out(R1), .sel(R_Addr1[4:3]));
endmodule

module Count (
  input  Reset,
  input  Clk,
  output [31:0] Count_out
);

  wire [31:0] adder_1_out;

  Adder #(.width(32)) adder_1 (.a(Count_out), .b({32{1'b0}}), .out(adder_1_out), .cin(1'b1));  // open: cout
  Register #(.width(32)) register_1 (.D(adder_1_out), .en(1'b1), .clk(Clk), .Q(Count_out), .clr(Reset));
endmodule

module ExControl (
  input  [1:0] ALUControl,
  input  Lui,
  input  [15:0] In_16,
  output [31:0] Out_32
);

  wire not_1_out, not_2_out, not_3_out, not_4_out;
  wire [1:0] and_2_out;

  not not_1 (not_1_out, ALUControl[0]);
  not not_2 (not_2_out, ALUControl[1]);
  not not_3 (not_3_out, ALUControl[0]);
  not not_4 (not_4_out, Lui);
  and and_1 (and_2_out[1], not_1_out, not_2_out, Lui);
  and and_2 (and_2_out[0], not_3_out, ALUControl[1], not_4_out);
  Multiplexer #(.select(2), .width(32)) multiplexer_1 (
    .in0({{17{In_16[15]}}, In_16[14:0]}), .in1({{16{1'b0}}, In_16}), .in2({In_16, {16{1'b0}}}), .out(Out_32),
    .sel(and_2_out));  // open: in3
endmodule

module Reg8_First (
  input  Clk,
  input  [31:0] W,
  input  WEn,
  input  [2:0] W_Addr,
  input  [2:0] R_Addr0,
  input  [2:0] R_Addr1,
  output [31:0] R0,
  output [31:0] R1
);

  wire demultiplexer_2_out0, demultiplexer_2_out1, demultiplexer_2_out2, demultiplexer_2_out3,
       demultiplexer_2_out4, demultiplexer_2_out5, demultiplexer_2_out6, demultiplexer_2_out7;
  wire [31:0] demultiplexer_1_out0, demultiplexer_1_out1, demultiplexer_1_out2, demultiplexer_1_out3,
       demultiplexer_1_out4, demultiplexer_1_out5, demultiplexer_1_out6, demultiplexer_1_out7,
       reg4byte_1_regout, reg4byte_2_regout, reg4byte_3_regout, reg4byte_4_regout, reg4byte_5_regout,
       reg4byte_6_regout, reg4byte_7_regout;

  Demultiplexer #(.select(3), .width(32)) demultiplexer_1 (
    .out0(demultiplexer_1_out0), .out1(demultiplexer_1_out1), .out2(demultiplexer_1_out2),
    .out3(demultiplexer_1_out3), .out4(demultiplexer_1_out4), .out5(demultiplexer_1_out5),
    .out6(demultiplexer_1_out6), .out7(demultiplexer_1_out7), .in(W), .sel(W_Addr));
  Demultiplexer #(.select(3)) demultiplexer_2 (
    .out0(demultiplexer_2_out0), .out1(demultiplexer_2_out1), .out2(demultiplexer_2_out2),
    .out3(demultiplexer_2_out3), .out4(demultiplexer_2_out4), .out5(demultiplexer_2_out5),
    .out6(demultiplexer_2_out6), .out7(demultiplexer_2_out7), .in(WEn), .sel(W_Addr));
  Reg4Byte reg4byte_1 (.clk(Clk), .WEn(demultiplexer_2_out1), .RegIn(demultiplexer_1_out1), .RegOut(reg4byte_1_regout));
  Reg4Byte reg4byte_2 (.clk(Clk), .WEn(demultiplexer_2_out2), .RegIn(demultiplexer_1_out2), .RegOut(reg4byte_2_regout));
  Reg4Byte reg4byte_3 (.clk(Clk), .WEn(demultiplexer_2_out3), .RegIn(demultiplexer_1_out3), .RegOut(reg4byte_3_regout));
  Reg4Byte reg4byte_4 (.clk(Clk), .WEn(demultiplexer_2_out4), .RegIn(demultiplexer_1_out4), .RegOut(reg4byte_4_regout));
  Reg4Byte reg4byte_5 (.clk(Clk), .WEn(demultiplexer_2_out5), .RegIn(demultiplexer_1_out5), .RegOut(reg4byte_5_regout));
  Reg4Byte reg4byte_6 (.clk(Clk), .WEn(demultiplexer_2_out6), .RegIn(demultiplexer_1_out6), .RegOut(reg4byte_6_regout));
  Reg4Byte reg4byte_7 (.clk(Clk), .WEn(demultiplexer_2_out7), .RegIn(demultiplexer_1_out7), .RegOut(reg4byte_7_regout));
  Multiplexer #(.select(3), .width(32)) multiplexer_1 (
    .in0({32{1'b0}}), .in1(reg4byte_1_regout), .in2(reg4byte_2_regout), .in3(reg4byte_3_regout),
    .in4(reg4byte_4_regout), .in5(reg4byte_5_regout), .in6(reg4byte_6_regout), .in7(reg4byte_7_regout),
    .out(R0), .sel(R_Addr0));
  Multiplexer #(.select(3), .width(32)) multiplexer_2 (
    .in0({32{1'b0}}), .in1(reg4byte_1_regout), .in2(reg4byte_2_regout), .in3(reg4byte_3_regout),
    .in4(reg4byte_4_regout), .in5(reg4byte_5_regout), .in6(reg4byte_6_regout), .in7(reg4byte_7_regout),
    .out(R1), .sel(R_Addr1));
endmodule

module BTB (
  input  Clk,
  input  [31:0] CMD_Addr,
  input  [31:0] CMD_In,
  input  [31:0] ID_R0,
  input  [31:0] ID_R1,
  input  Lu_Stall,
  output [31:0] CMD_Out,
  output [31:0] PC_NextAddr
);

  wire and_1_out, and_2_out, and_3_out, and_4_out, and_5_out, comparator_1_eq, comparator_2_eq, d_ff_1_q,
       d_ff_2_q, d_ff_3_q, d_ff_3_qn, not_1_out, not_2_out, not_3_out, or_1_out, xor_1_out;
  wire [1:0] btb_addr_1_data_out, or_2_out, ram_1_dout;
  wire [13:0] multiplexer_1_out, register_1_q;
  wire [31:0] adder_1_out, adder_2_out, bit_extender_1_out;
  wire [63:0] register_2_q;

  D_Flip_Flop d_ff_1 (.D(Lu_Stall), .clk(Clk), .Q(d_ff_1_q));  // open: Qn, preset, reset
  Register #(.width(14)) register_1 (.D(CMD_Addr[15:2]), .en(1'b1), .clk(and_1_out), .Q(register_1_q));  // open: clr
  not not_1 (not_1_out, or_1_out);
  D_Flip_Flop d_ff_2 (.D(comparator_2_eq), .clk(and_1_out), .Q(d_ff_2_q));  // open: Qn, preset, reset
  or or_1 (or_1_out, d_ff_1_q, Lu_Stall);
  Multiplexer #(.width(14)) multiplexer_1 (
    .in0(CMD_Addr[15:2]), .in1(register_1_q), .out(multiplexer_1_out), .sel(d_ff_2_q));
  and and_1 (and_1_out, Clk, not_1_out);
  assign bit_extender_1_out = {{16{CMD_In[15]}}, CMD_In[15:0]};  // Bit_Extender bit_extender_1
  not not_2 (not_2_out, comparator_1_eq);
  Comparator #(.mode("unsigned"), .width(32)) comparator_1 (
    .a(ID_R0), .b(ID_R1), .eq(comparator_1_eq));  // open: gt, lt
  Comparator #(.mode("unsigned"), .width(6)) comparator_2 (
    .a(CMD_In[31:26]), .b(6'b000101), .eq(comparator_2_eq));  // open: gt, lt
  Adder #(.width(32)) adder_1 (.a(32'h4), .b(CMD_Addr), .out(adder_1_out), .cin(1'b0));  // open: cout
  and and_2 (and_2_out, not_2_out, d_ff_2_q);
  RAM #(.addrWidth(14), .asyncread("true"), .dataWidth(2)) ram_1 (
    .addr(multiplexer_1_out), .we(d_ff_2_q), .oe(1'b1), .clk(and_1_out), .din(btb_addr_1_data_out),
    .dout(ram_1_dout));
  Adder #(.width(32)) adder_2 (
    .a(adder_1_out), .b({bit_extender_1_out[29:0], 2'b00}), .out(adder_2_out), .cin(1'b0));  // open: cout
  BTB_Addr btb_addr_1 (.Branch_Hit(not_3_out), .Data_In(ram_1_dout), .En(d_ff_2_q), .Data_Out(btb_addr_1_data_out));
  Register #(.width(64)) register_2 (
    .D({adder_2_out, adder_1_out}), .en(comparator_2_eq), .clk(and_1_out), .Q(register_2_q));  // open: clr
  D_Flip_Flop d_ff_3 (.D(and_3_out), .clk(and_1_out), .Q(d_ff_3_q), .Qn(d_ff_3_qn));  // open: preset, reset
  and and_3 (and_3_out, ram_1_dout[1], comparator_2_eq);
  not not_3 (not_3_out, xor_1_out);
  xor xor_1 (xor_1_out, d_ff_3_q, or_2_out[1]);
  xor Err_Detect (or_2_out[1], and_2_out, d_ff_3_q);
  and and_4 (and_4_out, d_ff_3_qn, or_2_out[1]);
  or or_2 (or_2_out[0], and_4_out, and_5_out);
  and and_5 (and_5_out, d_ff_3_qn, and_3_out);
  Multiplexer #(.width(32)) multiplexer_2 (.in0(CMD_In), .in1({32{1'b0}}), .out(CMD_Out), .sel(or_2_out[1]));
  Multiplexer #(.select(2), .width(32)) multiplexer_3 (
    .in0(adder_1_out), .in1(adder_2_out), .in2(register_2_q[31:0]), .in3(register_2_q[63:32]),
    .out(PC_NextAddr), .sel(or_2_out));
endmodule

module BTB_Addr (
  input  Branch_Hit,
  input  [1:0] Data_In,
  input  En,
  output [1:0] Data_Out
);

  wire and_1_out, and_2_out, and_3_out, and_4_out, and_5_out, and_6_out, not_1_out, not_2_out;
  wire [1:0] or_1_out;

  not not_1 (not_1_out, Data_In[0]);
  not not_2 (not_2_out, Branch_Hit);
  and and_1 (and_1_out, not_1_out, not_2_out);
  and and_2 (and_2_out, Data_In[1], not_2_out);
  and and_3 (and_3_out, not_1_out, Data_In[1]);
  and and_4 (and_4_out, Data_In[0], not_2_out);
  and and_5 (and_5_out, Data_In[1], not_2_out);
  and and_6 (and_6_out, Data_In[0], Data_In[1]);
  or or_1 (or_1_out[0], and_1_out, and_2_out, and_3_out);
  or or_2 (or_1_out[1], and_4_out, and_5_out, and_6_out);
  Multiplexer #(.width(2)) multiplexer_1 (.in0(Data_Out), .in1(or_1_out), .out(Data_Out), .sel(En));
endmodule
